// Logisim project somabits.circ as structural Verilog: 5 circuits, main circuit main
module main (
  input  in_1,
  input  in_2,
  input  in_3,
  input  [7:0] in_4,
  output out_5,
  output out_6,
  output [3:0] out_7
);

  wire undriven, undriven_2;
  wire [1:0] multiplexer_1_out;

  Multiplexer #(.width(2)) multiplexer_1 (.out(multiplexer_1_out), .sel(undriven), .en(undriven_2));  // open: in0, in1
  somabits somabits_1 (.a(in_1), .b(in_2), .cin(in_3), .s(out_5), .cout(out_6));

  assign out_7 = in_4[7:4];
endmodule

module \aritmética  (
  input  b0,
  input  b1,
  input  b2,
  input  b3,
  input  b4,
  input  b5,
  input  b6,
  input  b7,
  input  cin,
  input  a0,
  input  a1,
  input  a2,
  input  a3,
  input  a4,
  input  a5,
  input  a6,
  input  a7,
  output r0,
  output r1,
  output r2,
  output r3,
  output r4,
  output r5,
  output r6,
  output r7,
  output o0
);

  wire somabits_1_cout, somabits_2_cout, somabits_3_cout, somabits_4_cout, somabits_5_cout, somabits_6_cout,
       somabits_7_cout, somabits_8_cout;

  somabits somabits_1 (.a(a0), .b(b0), .cin(cin), .s(r0), .cout(somabits_1_cout));
  somabits somabits_2 (.a(a1), .b(b1), .cin(somabits_1_cout), .s(r1), .cout(somabits_2_cout));
  somabits somabits_3 (.a(a2), .b(b2), .cin(somabits_2_cout), .s(r2), .cout(somabits_3_cout));
  somabits somabits_4 (.a(a3), .b(b3), .cin(somabits_3_cout), .s(r3), .cout(somabits_4_cout));
  somabits somabits_5 (.a(a4), .b(b4), .cin(somabits_4_cout), .s(r4), .cout(somabits_5_cout));
  somabits somabits_6 (.a(a5), .b(b5), .cin(somabits_5_cout), .s(r5), .cout(somabits_6_cout));
  somabits somabits_7 (.a(a6), .b(b6), .cin(somabits_6_cout), .s(r6), .cout(somabits_7_cout));
  somabits somabits_8 (.a(a7), .b(b7), .cin(somabits_7_cout), .s(r7), .cout(somabits_8_cout));
  xor xor_1 (o0, somabits_7_cout, somabits_8_cout);
endmodule

module somabits (
  input  a,
  input  b,
  input  cin,
  output s,
  output cout
);

  wire and_1_out, and_2_out, xor_1_out;

  xor xor_1 (xor_1_out, a, b);
  and and_1 (and_1_out, a, b);
  and and_2 (and_2_out, xor_1_out, cin);
  xor xor_2 (s, xor_1_out, cin);
  or or_1 (cout, and_2_out, and_1_out);
endmodule

module aritmetica2 (
  input  [7:0] b,
  input  cin,
  input  [7:0] a,
  output r0,
  output r1,
  output r2,
  output r3,
  output r4,
  output r5,
  output r6,
  output r7,
  output o0
);

  wire somabits_1_cout, somabits_2_cout, somabits_3_cout, somabits_4_cout, somabits_5_cout, somabits_6_cout,
       somabits_7_cout, somabits_8_cout;

  somabits somabits_1 (.a(a[0]), .b(b[0]), .cin(cin), .s(r0), .cout(somabits_1_cout));
  somabits somabits_2 (.a(a[1]), .b(b[1]), .cin(somabits_1_cout), .s(r1), .cout(somabits_2_cout));
  somabits somabits_3 (.a(a[2]), .b(b[2]), .cin(somabits_2_cout), .s(r2), .cout(somabits_3_cout));
  somabits somabits_4 (.a(a[3]), .b(b[3]), .cin(somabits_3_cout), .s(r3), .cout(somabits_4_cout));
  somabits somabits_5 (.cin(somabits_4_cout), .s(r4), .cout(somabits_5_cout));  // open: a, b
  somabits somabits_6 (.cin(somabits_5_cout), .s(r5), .cout(somabits_6_cout));  // open: a, b
  somabits somabits_7 (.cin(somabits_6_cout), .s(r6), .cout(somabits_7_cout));  // open: a, b
  somabits somabits_8 (.cin(somabits_7_cout), .s(r7), .cout(somabits_8_cout));  // open: a, b
  xor xor_1 (o0, somabits_7_cout, somabits_8_cout);
endmodule

module comparar (
  input  a0,
  input  a1,
  input  a2,
  input  a3,
  input  a4,
  input  a5,
  input  a6,
  input  a7,
  output f1
);
endmodule
