// Logisim project projeto1.circ as structural Verilog: 6 circuits, main circuit main
module main (
  input  a7,
  input  a6,
  input  a5,
  input  a4,
  input  a3,
  input  a2,
  input  a1,
  input  a0,
  input  b7,
  input  b6,
  input  b5,
  input  b4,
  input  b3,
  input  b2,
  input  b1,
  input  b0,
  input  s0,
  input  s1,
  output o0,
  output o1,
  output o2,
  output o3,
  output r7,
  output r6,
  output r5,
  output r4,
  output r3,
  output r2,
  output r1,
  output r0
);

  ula ula_1 (
    .s0(s0), .s1(s1), .o0(o0), .o1(o1), .o2(o2), .o3(o3), .a7(a7), .a6(a6), .a5(a5), .a4(a4), .a3(a3),
    .a2(a2), .a1(a1), .a0(a0), .b7(b7), .b6(b6), .b5(b5), .b4(b4), .b3(b3), .b2(b2), .b1(b1), .b0(b0),
    .r7(r7), .r6(r6), .r5(r5), .r4(r4), .r3(r3), .r2(r2), .r1(r1), .r0(r0));

  // Notes on the sheet:
  //   S
  //   A
  //   R
  //   B
  //   Flags
endmodule

module soma_bits (
  input  a,
  input  b,
  input  cin,
  output s,
  output cout
);

  wire and_1_out, and_2_out, xor_1_out;

  xor xor_1 (xor_1_out, a, b);
  and and_1 (and_1_out, a, b);
  and and_2 (and_2_out, xor_1_out, cin);
  xor xor_2 (s, xor_1_out, cin);
  or or_1 (cout, and_2_out, and_1_out);
endmodule

// ARITMÉTICA
module soma_8_bits (
  input  b0,
  input  b1,
  input  b2,
  input  b3,
  input  b4,
  input  b5,
  input  b6,
  input  b7,
  input  a0,
  input  a1,
  input  a2,
  input  a3,
  input  a4,
  input  a5,
  input  a6,
  input  a7,
  input  cin_inicial,
  output o0,
  output r0,
  output r1,
  output r2,
  output r3,
  output r4,
  output r5,
  output r6,
  output r7
);

  wire soma_bits_1_cout, soma_bits_2_cout, soma_bits_3_cout, soma_bits_4_cout, soma_bits_5_cout,
       soma_bits_6_cout, soma_bits_7_cout, soma_bits_8_cout;

  soma_bits soma_bits_1 (.a(a0), .b(b0), .cin(cin_inicial), .s(r0), .cout(soma_bits_1_cout));
  soma_bits soma_bits_2 (.a(a1), .b(b1), .cin(soma_bits_1_cout), .s(r1), .cout(soma_bits_2_cout));
  soma_bits soma_bits_3 (.a(a2), .b(b2), .cin(soma_bits_2_cout), .s(r2), .cout(soma_bits_3_cout));
  soma_bits soma_bits_4 (.a(a3), .b(b3), .cin(soma_bits_3_cout), .s(r3), .cout(soma_bits_4_cout));
  soma_bits soma_bits_5 (.a(a4), .b(b4), .cin(soma_bits_4_cout), .s(r4), .cout(soma_bits_5_cout));
  soma_bits soma_bits_6 (.a(a5), .b(b5), .cin(soma_bits_5_cout), .s(r5), .cout(soma_bits_6_cout));
  soma_bits soma_bits_7 (.a(a6), .b(b6), .cin(soma_bits_6_cout), .s(r6), .cout(soma_bits_7_cout));
  soma_bits soma_bits_8 (.a(a7), .b(b7), .cin(soma_bits_7_cout), .s(r7), .cout(soma_bits_8_cout));
  xor xor_1 (o0, soma_bits_7_cout, soma_bits_8_cout);
endmodule

// COMPLEMENTO
module \complemento_de_binário  (
  input  b0,
  input  b1,
  input  b2,
  input  b3,
  input  b4,
  input  b5,
  input  b6,
  input  b7,
  input  s0,
  output nb0,
  output nb1,
  output nb2,
  output nb3,
  output nb4,
  output nb5,
  output nb6,
  output nb7
);

  xor xor_1 (nb0, b0, s0);
  xor xor_2 (nb1, b1, s0);
  xor xor_3 (nb2, b2, s0);
  xor xor_4 (nb3, b3, s0);
  xor xor_5 (nb4, b4, s0);
  xor xor_6 (nb5, b5, s0);
  xor xor_7 (nb6, b6, s0);
  xor xor_8 (nb7, b7, s0);
endmodule

// COMPARAÇÃO
module \comparação  (
  input  a0,
  input  a1,
  input  a2,
  input  a3,
  input  a4,
  input  a5,
  input  a6,
  input  a7,
  output o1,
  output o2,
  output o3
);

  wire or_1_out, or_2_out;

  or or_1 (or_1_out, a0, a1, a2, a3, a4, a5, a6, a7);
  not not_1 (o2, or_1_out);
  or or_2 (or_2_out, o2, a7);
  not not_2 (o3, or_2_out);

  assign o1 = a7;
endmodule

// ULA
module ula (
  input  b7,
  input  b6,
  input  b5,
  input  b4,
  input  b3,
  input  b2,
  input  b1,
  input  b0,
  input  a7,
  input  a6,
  input  a5,
  input  a4,
  input  a3,
  input  a2,
  input  a1,
  input  a0,
  input  s0,
  input  s1,
  output o0,
  output o1,
  output o2,
  output o3,
  output r7,
  output r6,
  output r5,
  output r4,
  output r3,
  output r2,
  output r1,
  output r0
);

  wire \complemento_de_binário_1_nb0 , \complemento_de_binário_1_nb1 , \complemento_de_binário_1_nb2 ,
       \complemento_de_binário_1_nb3 , \complemento_de_binário_1_nb4 , \complemento_de_binário_1_nb5 ,
       \complemento_de_binário_1_nb6 , \complemento_de_binário_1_nb7 ;

  \comparação  \comparação_1  (
    .a0(a0), .a1(a1), .a2(a2), .a3(a3), .a4(a4), .a5(a5), .a6(a6), .a7(a7), .o1(o1), .o2(o2), .o3(o3));
  soma_8_bits soma_8_bits_1 (
    .b0(\complemento_de_binário_1_nb0 ), .b1(\complemento_de_binário_1_nb1 ),
    .b2(\complemento_de_binário_1_nb2 ), .b3(\complemento_de_binário_1_nb3 ),
    .b4(\complemento_de_binário_1_nb4 ), .b5(\complemento_de_binário_1_nb5 ),
    .b6(\complemento_de_binário_1_nb6 ), .b7(\complemento_de_binário_1_nb7 ), .a0(a0), .a1(a1), .a2(a2),
    .a3(a3), .a4(a4), .a5(a5), .a6(a6), .a7(a7), .cin_inicial(s0), .o0(o0), .r0(r0), .r1(r1), .r2(r2),
    .r3(r3), .r4(r4), .r5(r5), .r6(r6), .r7(r7));
  \complemento_de_binário  \complemento_de_binário_1  (
    .b0(b0), .b1(b1), .b2(b2), .b3(b3), .b4(b4), .b5(b5), .b6(b6), .b7(b7),
    .nb0(\complemento_de_binário_1_nb0 ), .nb1(\complemento_de_binário_1_nb1 ),
    .nb2(\complemento_de_binário_1_nb2 ), .nb3(\complemento_de_binário_1_nb3 ),
    .nb4(\complemento_de_binário_1_nb4 ), .nb5(\complemento_de_binário_1_nb5 ),
    .nb6(\complemento_de_binário_1_nb6 ), .nb7(\complemento_de_binário_1_nb7 ), .s0(s0));
endmodule
