// Logisim project projeto2.circ as structural Verilog: 3 circuits, main circuit main
module main (
  input  [15:0] Input,
  input  C_inc,
  input  Clear,
  input  in_4,
  input  in_5,
  input  in_6,
  input  in_7,
  input  in_8,
  input  in_9,
  input  in_10,
  output [7:0] \Endereço ,
  output [7:0] \Instrução ,
  output out_13,
  output out_14,
  output out_15
);

  wire and_1_out, c, clock_1_out, \Controle__1_se_se_acc_for_menor_que_0__desviar_o_endereço_da_memória ,
       \Controle__1_se_é_para_copiar_da_acc_para_memória , \Controle__1_se_é_para_copiar_da_mmória_para_acc ,
       \Controle__1_se_é_para_copiar_o_input_na_memoria , \Controle__1_se_é_para_imprimir_da_memória ,
       \Controle__1_se_é_para_parar ,
       \Controle__1_se_é_para_somar_o_acc_com_o_endereço_na_memória_e_copar_em_acc , j_k_ff_1_q, nor_1_out,
       not_1_out, not_2_out, or_1_out, or_2_out, or_3_out;
  wire [7:0] b, demultiplexer_2_out1, multiplexer_2_out, PC_q;
  wire [15:0] ACC_q, controlled_buffer_1_out, demultiplexer_2_out0, \uc_1_saída__cópia_da_entrada ;

  not not_1 (not_1_out, \Controle__1_se_é_para_parar );
  Clock clock_1 (.out(clock_1_out));
  not not_2 (not_2_out, c);
  and and_1 (and_1_out, not_1_out, not_2_out, C_inc);
  J_K_Flip_Flop j_k_ff_1 (.J(C_inc), .clk(clock_1_out), .K(C_inc), .Q(j_k_ff_1_q));  // open: Qn, preset, en, reset
  Counter #(.trigger("falling")) PC (
    .load(c), .D(b), .count(and_1_out), .Q(PC_q), .clk(j_k_ff_1_q), .clr(Clear));  // open: carry
  Multiplexer multiplexer_1 (.in0(in_4), .in1(in_5), .out(out_14), .sel(in_7), .en(in_8));
  Multiplexer #(.width(8)) multiplexer_2 (
    .in0(PC_q), .in1(\Endereço ), .out(multiplexer_2_out), .sel(or_1_out), .en(1'b1));
  or or_1 (or_1_out, \Controle__1_se_é_para_copiar_o_input_na_memoria , \Controle__1_se_é_para_copiar_da_mmória_para_acc , \Controle__1_se_é_para_copiar_da_acc_para_memória );
  assign controlled_buffer_1_out = \Controle__1_se_é_para_copiar_o_input_na_memoria  ? Input : 16'bz;  // Controlled_Buffer controlled_buffer_1
  Demultiplexer demultiplexer_1 (.out0(out_13), .out1(out_15), .in(in_6), .sel(in_10), .en(in_9));
  RAM #(.dataWidth(16)) ram_1 (
    .addr(multiplexer_2_out), .data(controlled_buffer_1_out), .clk(clock_1_out), .ld(or_2_out));  // open: sel, clr
  or or_2 (or_2_out, nor_1_out, \Controle__1_se_é_para_imprimir_da_memória );
  nor nor_1 (nor_1_out, \Controle__1_se_é_para_copiar_da_acc_para_memória , \Controle__1_se_é_para_copiar_o_input_na_memoria );
  Demultiplexer #(.width(16)) demultiplexer_2 (
    .out0(demultiplexer_2_out0), .out1({demultiplexer_2_out1, b}), .in(controlled_buffer_1_out),
    .sel(or_3_out), .en(1'b1));
  or or_3 (or_3_out, \Controle__1_se_é_para_copiar_da_mmória_para_acc , c, \Controle__1_se_é_para_copiar_da_acc_para_memória );
  Hex_Digit_Display hex_digit_display_1 (.value(demultiplexer_2_out1[7:4]));  // open: dp
  UC uc_1 (.Entrada(demultiplexer_2_out0), .\Saída__cópia_da_entrada (\uc_1_saída__cópia_da_entrada ));
  assign controlled_buffer_1_out = \Controle__1_se_é_para_copiar_da_acc_para_memória  ? ACC_q : 16'bz;  // Controlled_Buffer controlled_buffer_2
  Register #(.width(16)) ACC (
    .D({demultiplexer_2_out1, b}), .en(\Controle__1_se_é_para_copiar_da_mmória_para_acc ), .Q(ACC_q),
    .clk(clock_1_out), .clr(Clear));
  Hex_Digit_Display hex_digit_display_2 (.value(demultiplexer_2_out1[3:0]));  // open: dp
  Register #(.width(16)) IR (
    .D(\uc_1_saída__cópia_da_entrada ), .Q({\Instrução , \Endereço }), .clk(clock_1_out), .clr(Clear));  // open: en
  Hex_Digit_Display hex_digit_display_3 (.value(b[7:4]));  // open: dp
  Controle Controle (
    .\_1_se_é_para_copiar_da_mmória_para_ACC (\Controle__1_se_é_para_copiar_da_mmória_para_acc ),
    .\_1_se_é_para_copiar_da_ACC_para_memória (\Controle__1_se_é_para_copiar_da_acc_para_memória ),
    .\_1_se_é_para_copiar_o_input_na_memoria (\Controle__1_se_é_para_copiar_o_input_na_memoria ),
    .\_1_se_é_para_imprimir_da_memória (\Controle__1_se_é_para_imprimir_da_memória ),
    .\_1_se_é_para_somar_o_ACC_com_o_endereço_na_memória_e_copar_em_ACC (\Controle__1_se_é_para_somar_o_acc_com_o_endereço_na_memória_e_copar_em_acc ),
    .\_1_se_é_para_desviar_o_endereço_da_memória (c),
    .\_1_se_se_ACC_for_menor_que_0__desviar_o_endereço_da_memória (\Controle__1_se_se_acc_for_menor_que_0__desviar_o_endereço_da_memória ),
    .\_1_se_é_para_parar (\Controle__1_se_é_para_parar ), .in_1(\Instrução ));
  Hex_Digit_Display hex_digit_display_4 (.value(b[3:0]));  // open: dp

  // Other names for the same wires on the sheet: a = Clear
endmodule

module UC (
  input  [15:0] Entrada,
  output [15:0] \Saída__cópia_da_entrada 
);


  assign \Saída__cópia_da_entrada  = Entrada;
endmodule

module Controle (
  input  [7:0] in_1,
  output \_1_se_é_para_copiar_da_mmória_para_ACC ,
  output \_1_se_é_para_copiar_da_ACC_para_memória ,
  output \_1_se_é_para_copiar_o_input_na_memoria ,
  output \_1_se_é_para_imprimir_da_memória ,
  output \_1_se_é_para_somar_o_ACC_com_o_endereço_na_memória_e_copar_em_ACC ,
  output \_1_se_é_para_desviar_o_endereço_da_memória ,
  output \_1_se_se_ACC_for_menor_que_0__desviar_o_endereço_da_memória ,
  output \_1_se_é_para_parar 
);

  wire not_1_out, not_2_out, not_3_out, not_4_out, not_5_out, not_6_out, not_7_out, not_8_out, not_9_out,
       not_10_out, not_11_out, not_12_out, not_13_out, not_14_out, not_15_out, not_16_out, not_17_out,
       not_18_out, not_19_out, not_20_out, not_21_out, not_22_out, not_23_out, not_24_out, not_25_out,
       not_26_out, not_27_out, not_28_out, not_29_out, not_30_out, not_31_out, not_32_out, not_33_out,
       not_34_out, not_35_out, not_36_out, not_37_out, not_38_out;

  not not_1 (not_1_out, in_1[6]);
  not not_2 (not_2_out, in_1[5]);
  not not_3 (not_3_out, in_1[7]);
  not not_4 (not_4_out, in_1[4]);
  not not_5 (not_5_out, in_1[2]);
  and and_1 (\_1_se_é_para_copiar_da_mmória_para_ACC , not_3_out, not_1_out, not_2_out, not_4_out, in_1[3], not_5_out, in_1[1], in_1[0]);
  not not_6 (not_6_out, in_1[7]);
  not not_7 (not_7_out, in_1[5]);
  not not_8 (not_8_out, in_1[6]);
  not not_9 (not_9_out, in_1[4]);
  and and_2 (\_1_se_é_para_copiar_da_ACC_para_memória , not_6_out, not_8_out, not_7_out, not_9_out, in_1[3], in_1[2], not_13_out, not_10_out);
  not not_10 (not_10_out, in_1[0]);
  not not_11 (not_11_out, in_1[7]);
  not not_12 (not_12_out, in_1[6]);
  not not_13 (not_13_out, in_1[1]);
  not not_14 (not_14_out, in_1[5]);
  and and_3 (\_1_se_é_para_copiar_o_input_na_memoria , not_11_out, not_12_out, not_14_out, in_1[4], in_1[3], in_1[2], in_1[1], in_1[0]);
  not not_15 (not_15_out, in_1[7]);
  not not_16 (not_16_out, in_1[4]);
  not not_17 (not_17_out, in_1[6]);
  and and_4 (\_1_se_é_para_imprimir_da_memória , not_15_out, not_17_out, in_1[5], not_16_out, in_1[3], not_18_out, not_19_out, in_1[0]);
  not not_18 (not_18_out, in_1[2]);
  not not_19 (not_19_out, in_1[1]);
  not not_20 (not_20_out, in_1[7]);
  not not_21 (not_21_out, in_1[5]);
  not not_22 (not_22_out, in_1[6]);
  not not_23 (not_23_out, in_1[3]);
  and and_5 (\_1_se_é_para_somar_o_ACC_com_o_endereço_na_memória_e_copar_em_ACC , not_20_out, not_22_out, not_21_out, in_1[4], not_23_out, in_1[2], not_24_out, in_1[0]);
  not not_24 (not_24_out, in_1[1]);
  not not_25 (not_25_out, in_1[6]);
  not not_26 (not_26_out, in_1[7]);
  and and_6 (\_1_se_é_para_desviar_o_endereço_da_memória , not_26_out, not_25_out, in_1[5], in_1[4], not_27_out, not_28_out, in_1[1], in_1[0]);
  not not_27 (not_27_out, in_1[3]);
  not not_28 (not_28_out, in_1[2]);
  not not_29 (not_29_out, in_1[7]);
  not not_30 (not_30_out, in_1[6]);
  not not_31 (not_31_out, in_1[1]);
  not not_32 (not_32_out, in_1[2]);
  and and_7 (\_1_se_se_ACC_for_menor_que_0__desviar_o_endereço_da_memória , not_29_out, not_30_out, in_1[5], in_1[4], in_1[3], not_32_out, not_31_out, not_33_out);
  not not_33 (not_33_out, in_1[0]);
  not not_34 (not_34_out, in_1[7]);
  not not_35 (not_35_out, in_1[4]);
  not not_36 (not_36_out, in_1[3]);
  not not_37 (not_37_out, in_1[5]);
  and and_8 (\_1_se_é_para_parar , not_34_out, in_1[6], not_37_out, not_35_out, not_36_out, in_1[2], in_1[1], not_38_out);
  not not_38 (not_38_out, in_1[0]);
endmodule
