// Logisim project ex10-lista1.circ as structural Verilog: 1 circuit, main circuit main
module main (
  input  in_1,
  input  in_2,
  input  in_3,
  output out_4
);

  wire and_1_out, not_1_out, not_2_out, or_1_out;

  not not_1 (not_1_out, in_1);
  and and_1 (and_1_out, not_1_out, not_1_out, in_2, in_2);
  or or_1 (or_1_out, in_1, in_3);
  not not_2 (not_2_out, or_1_out);
  or or_2 (out_4, and_1_out, not_2_out);
endmodule
